# Fritzing sketch pedalproto1 (saved by Fritzing 0.9.10b)
circuit board: 8.46667cm x 5.64444cm
breadboards: 1

parts:
  ADC1 = MCP3008 [package=dil16]
  U1 = POT [knob_status=50% power=0.5W package=pot_alpha_rv16af-20]
  U2 = POT [knob_status=50% power=0.5W package=pot_alpha_rv16af-20]
  U3 = POT [knob_status=50% power=0.5W package=pot_alpha_rv16af-20]
  U4 = POT [knob_status=50% power=0.5W package=pot_alpha_rv16af-20]
  Pro_Micro = Arduino Pro Mini v13
  S1 = Round Pushbutton
  S2 = Round Pushbutton
  S3 = Round Pushbutton
  S4 = Round Pushbutton

nets:
  N1: ADC1.CH0, U1.S
  N2: ADC1.CH1, U2.S
  N3: ADC1.CH2, U3.S
  N4: ADC1.CH3, U4.S
  N5: ADC1.DGND, ADC1.AGND, U1.E, U2.E, U3.E, U4.E, Pro_Micro.GND
  N6: ADC1.CS/SHDN, Pro_Micro.D10_PWM/SS
  N7: ADC1.Din, Pro_Micro.D11_PWM/MOSI
  N8: ADC1.Dout, Pro_Micro.D12/MISO
  N9: ADC1.CLK, Pro_Micro.D13/SCK
  VDD: ADC1.VREF, ADC1.VDD, U1.A, U2.A, U3.A, U4.A, Pro_Micro.VCC, S1.leg0, S2.leg0, S3.leg0
  N10: Pro_Micro.D5_PWM, S4.leg1
  N11: Pro_Micro.D4, S3.leg1
  N12: Pro_Micro.D3_PWM, S2.leg1
  N13: Pro_Micro.D2, S1.leg1
